// Logisim project circuito_ShiftLeft.circ as structural Verilog: 3 circuits, main circuit main
module main (
  input  [15:0] A,
  output [15:0] B,
  output carry
);

  or or_1 (carry, A[15], 1'b0);
  or or_2 (B[15], A[14], 1'b0);
  or or_3 (B[14], A[13], 1'b0);
  or or_4 (B[13], A[12], 1'b0);
  or or_5 (B[11], A[10], 1'b0);
  or or_6 (B[12], A[11], 1'b0);
  or or_7 (B[10], A[9], 1'b0);
  or or_8 (B[9], A[8], 1'b0);
  or or_9 (B[8], A[7], 1'b0);
  or or_10 (B[7], A[6], 1'b0);
  or or_11 (B[6], A[5], 1'b0);
  or or_12 (B[5], A[4], 1'b0);
  or or_13 (B[4], A[3], 1'b0);
  or or_14 (B[3], A[2], 1'b0);
  or or_15 (B[2], A[1], 1'b0);
  or or_16 (B[1], A[0], 1'b0);
  or or_17 (B[0], 1'b0, 1'b0);
endmodule

module ShiftLeft16 (
  input  [15:0] A,
  output [15:0] B,
  output carry
);

  or or_1 (carry, A[15], 1'b0);
  or or_2 (B[15], A[14], 1'b0);
  or or_3 (B[14], A[13], 1'b0);
  or or_4 (B[13], A[12], 1'b0);
  or or_5 (B[11], A[10], 1'b0);
  or or_6 (B[12], A[11], 1'b0);
  or or_7 (B[10], A[9], 1'b0);
  or or_8 (B[9], A[8], 1'b0);
  or or_9 (B[8], A[7], 1'b0);
  or or_10 (B[7], A[6], 1'b0);
  or or_11 (B[6], A[5], 1'b0);
  or or_12 (B[5], A[4], 1'b0);
  or or_13 (B[4], A[3], 1'b0);
  or or_14 (B[3], A[2], 1'b0);
  or or_15 (B[2], A[1], 1'b0);
  or or_16 (B[1], A[0], 1'b0);
  or or_17 (B[0], 1'b0, 1'b0);
endmodule

module ShiftLeft64 (
  input  [63:0] A,
  output [63:0] B
);

  wire [0:0] shiftleft16_2_b, shiftleft16_3_b, shiftleft16_4_b;

  ShiftLeft16 shiftleft16_1 (.A(A[15:0]), .B(B[15:0]), .carry(B[16]));
  ShiftLeft16 shiftleft16_2 (.A(A[31:16]), .B({B[31:17], shiftleft16_2_b[0]}), .carry(B[32]));
  ShiftLeft16 shiftleft16_3 (.A(A[47:32]), .B({B[47:33], shiftleft16_3_b[0]}), .carry(B[48]));
  ShiftLeft16 shiftleft16_4 (.A(A[63:48]), .B({B[63:49], shiftleft16_4_b[0]}));  // open: carry
endmodule
